# Fritzing sketch Note-Taker Circuit Diagram (saved by Fritzing 0.9.9b)
breadboards: 1

parts:
  Raspberry_Pi_Pico = Raspberry Pi Pico
  RFID-RC522 = mystery part, 8 pins [chip_label="RFID Reader"]
  Screen = mystery part, 4 pins [chip_label=LCD]
  Rotary_Encoder = mystery part, 5 pins [chip_label="Rtry Encdr"]
  Button = mystery part, 2 pins [chip_label=Btn]

nets:
  N1: Raspberry_Pi_Pico.pin_3, Raspberry_Pi_Pico.pin_8, Raspberry_Pi_Pico.pin_13, Raspberry_Pi_Pico.pin_18, Raspberry_Pi_Pico.pin_23, Raspberry_Pi_Pico.pin_28, Raspberry_Pi_Pico.pin_33, Raspberry_Pi_Pico.pin_38
  N2: Raspberry_Pi_Pico.pin_6, Screen.pin4
  N3: Raspberry_Pi_Pico.pin_7, Screen.pin3
  N4: Raspberry_Pi_Pico.pin_11, RFID-RC522.pin5
  N5: Raspberry_Pi_Pico.pin_16, RFID-RC522.pin7
  N6: Raspberry_Pi_Pico.pin_17, RFID-RC522.pin2
  N7: Raspberry_Pi_Pico.pin_19, RFID-RC522.pin3
  N8: Raspberry_Pi_Pico.pin_20, RFID-RC522.pin4
  N9: Raspberry_Pi_Pico.pin_21, Rotary_Encoder.pin3
  N10: Raspberry_Pi_Pico.pin_22, Button.pin2
  N11: Raspberry_Pi_Pico.pin_24, Rotary_Encoder.pin2
  N12: Raspberry_Pi_Pico.pin_25, Rotary_Encoder.pin1
  GND: RFID-RC522.pin6, Screen.pin2, Rotary_Encoder.pin5, Button.pin1
  3.3V: RFID-RC522.pin8, Screen.pin1, Rotary_Encoder.pin4

custom parts:
  Raspberry Pi Pico: Raspberry Pi Pico. Based around the RP2040 microcontroller the Pico is a low cost microcontroller device bringing Raspberry Pi quality, cost, and easy of use to the microcontroller space. Jan 2021, Split part in to two versions: tht (this one) and SMD. This one will drill holes for a .1 in header in pcb to allow plugging in the module as well as providing pads to solder the module to the top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
